# Fritzing sketch A600-keyboard-interface (saved by Fritzing 0.8.7b)
circuit board: 7.98517cm x 2.99049cm
breadboards: 1

parts:
  J1_ODD = female pin header, 15 pins [form="♀ (female)"]
  J1_EVEN = female pin header, 15 pins [form="♀ (female)"]
  R1 = Resistor [tolerance=±5% resistance=220 package=THT]
  IC1 = IC, DIP package, 28 pins [chip_label=MCP23017]
  IC2 = IC, DIP package, 28 pins [chip_label=MCP23017]
  J2 = female pin header, 4 pins [form="♀ (female)"]
  J3 = female pin header, 3 pins [form="♀ (female)"]
  J4 = female pin header, 3 pins [form="♀ (female)"]

nets:
  N1: J1_ODD.pin1, IC1.pin5
  N2: J1_ODD.pin2, IC1.pin4
  N3: J1_ODD.pin3, IC1.pin2
  N4: J1_ODD.pin4, IC1.pin1
  N5: J1_ODD.pin5, R1.Pin_0
  N6: J1_ODD.pin6, IC1.pin26
  N7: J1_ODD.pin7, IC1.pin28
  N8: J1_ODD.pin8, IC2.pin28
  N9: J1_ODD.pin9, IC2.pin27
  N10: J1_ODD.pin10, IC2.pin26
  N11: J1_ODD.pin11, IC2.pin25
  N12: J1_ODD.pin12, IC2.pin24
  N13: J1_ODD.pin13, IC2.pin23
  N14: J1_ODD.pin14, IC2.pin22
  N15: J1_ODD.pin15, IC2.pin21
  N16: J1_EVEN.pin1, IC1.pin3
  N17: J1_EVEN.pin2, IC1.pin8
  N18: J1_EVEN.pin3, IC1.pin23
  N19: J1_EVEN.pin4, IC1.pin24
  N20: J1_EVEN.pin5, IC1.pin25
  N21: J1_EVEN.pin6, IC1.pin27
  N22: J1_EVEN.pin7, IC2.pin1
  N23: J1_EVEN.pin8, IC2.pin2
  N24: J1_EVEN.pin9, IC2.pin3
  N25: J1_EVEN.pin10, IC2.pin4
  N26: J1_EVEN.pin11, IC2.pin5
  N27: J1_EVEN.pin12, IC2.pin6
  N28: J1_EVEN.pin13, IC2.pin7
  N29: J1_EVEN.pin14, IC2.pin8
  N30: J1_EVEN.pin15, IC1.pin6
  N31: R1.Pin_1, IC1.pin9, IC2.pin9, IC2.pin15, J2.pin1, J3.pin1, J4.pin1
  N32: IC1.pin10, IC1.pin15, IC2.pin10, J2.pin2, J3.pin3, J4.pin3
  N33: IC1.pin12, IC2.pin12, J2.pin3
  N34: IC1.pin13, IC2.pin13, J2.pin4
  N35: IC1.pin16, J3.pin2
  N36: IC1.pin17, J4.pin2

notes:
  2
  29
  30
  1
